// Logisim project flip-flops.circ as structural Verilog: 8 circuits, main circuit main
module main (
);

  \Flip_Flop_RS_Básico  \ff_rs_básico_1  ();
endmodule

module \Flip_Flop_RS_Básico  (
);

  wire nand_1_out, nand_2_out, not_1_out, not_2_out, RESET_out, SET_out;

  Button SET (.out(SET_out));
  Button RESET (.out(RESET_out));
  not not_1 (not_1_out, SET_out);
  not not_2 (not_2_out, RESET_out);
  nand nand_1 (nand_1_out, not_1_out, nand_2_out);
  nand nand_2 (nand_2_out, nand_1_out, not_2_out);
  LED Q (.in(nand_1_out));
  LED Q_2 (.in(nand_2_out));
endmodule

module Flip_Flop_RS_Clock (
);

  wire CLK_out, nand_1_out, nand_2_out, nand_3_out, nand_4_out, RESET_out, SET_out;

  Button SET (.out(SET_out));
  Clock CLK (.out(CLK_out));
  Button RESET (.out(RESET_out));
  nand nand_1 (nand_1_out, SET_out, CLK_out);
  nand nand_2 (nand_2_out, CLK_out, RESET_out);
  nand nand_3 (nand_3_out, nand_1_out, nand_4_out);
  nand nand_4 (nand_4_out, nand_3_out, nand_2_out);
  LED Q (.in(nand_3_out));
  LED Q_2 (.in(nand_4_out));
endmodule

module Flip_Flop_RS_Master_Slave (
);

  wire clock_1_out, nand_1_out, nand_2_out, nand_3_out, nand_4_out, nand_5_out, nand_6_out, nand_7_out,
       nand_8_out, not_1_out, RESET_out, SET_out;

  Button SET (.out(SET_out));
  Clock clock_1 (.out(clock_1_out));
  Button RESET (.out(RESET_out));
  nand nand_1 (nand_1_out, SET_out, clock_1_out);
  nand nand_2 (nand_2_out, clock_1_out, RESET_out);
  nand nand_3 (nand_3_out, nand_1_out, nand_4_out);
  nand nand_4 (nand_4_out, nand_3_out, nand_2_out);
  not not_1 (not_1_out, clock_1_out);
  nand nand_5 (nand_5_out, nand_3_out, not_1_out);
  nand nand_6 (nand_6_out, nand_5_out, nand_8_out);
  nand nand_7 (nand_7_out, not_1_out, nand_4_out);
  nand nand_8 (nand_8_out, nand_6_out, nand_7_out);
  LED Q (.in(nand_6_out));
  LED Q_2 (.in(nand_8_out));
endmodule

module Flip_Flop_RS_MS_PRE_CLR (
);

  wire CLEAR_out, clock_1_out, nand_1_out, nand_2_out, nand_3_out, nand_4_out, nand_5_out, nand_6_out,
       nand_7_out, nand_8_out, not_1_out, not_2_out, not_3_out, PRESET_out, RESET_out, SET_out;

  Button PRESET (.out(PRESET_out));
  Button SET (.out(SET_out));
  Clock clock_1 (.out(clock_1_out));
  Button RESET (.out(RESET_out));
  Button CLEAR (.out(CLEAR_out));
  not not_1 (not_1_out, PRESET_out);
  not not_2 (not_2_out, CLEAR_out);
  nand nand_1 (nand_1_out, SET_out, not_2_out, clock_1_out);
  nand nand_2 (nand_2_out, clock_1_out, not_1_out, RESET_out);
  nand nand_3 (nand_3_out, not_1_out, nand_1_out, nand_4_out);
  not not_3 (not_3_out, clock_1_out);
  nand nand_4 (nand_4_out, nand_3_out, nand_2_out, not_2_out);
  nand nand_5 (nand_5_out, not_1_out, nand_6_out, nand_8_out);
  nand nand_6 (nand_6_out, not_2_out, nand_3_out, not_3_out);
  nand nand_7 (nand_7_out, not_3_out, nand_4_out, not_1_out);
  nand nand_8 (nand_8_out, nand_5_out, nand_7_out, not_2_out);
  LED Q (.in(nand_5_out));
  LED Q_2 (.in(nand_8_out));
endmodule

module Flip_Flop_JK (
  input  JUMP,
  input  KILL
);

  wire CLEAR_out, clock_1_out, nand_1_out, nand_2_out, nand_3_out, nand_4_out, nand_5_out, nand_6_out,
       nand_7_out, nand_8_out, not_1_out, not_2_out, not_3_out, PRESET_out;

  Clock clock_1 (.out(clock_1_out));
  Button PRESET (.out(PRESET_out));
  not not_1 (not_1_out, PRESET_out);
  nand nand_1 (nand_1_out, nand_7_out, JUMP, clock_1_out);
  nand nand_2 (nand_2_out, clock_1_out, KILL, nand_5_out);
  not not_2 (not_2_out, CLEAR_out);
  Button CLEAR (.out(CLEAR_out));
  nand nand_3 (nand_3_out, not_1_out, nand_1_out, nand_4_out);
  not not_3 (not_3_out, clock_1_out);
  nand nand_4 (nand_4_out, nand_3_out, nand_2_out, not_2_out);
  nand nand_5 (nand_5_out, not_1_out, nand_6_out, nand_7_out);
  nand nand_6 (nand_6_out, not_2_out, nand_3_out, not_3_out);
  nand nand_7 (nand_7_out, nand_5_out, nand_8_out, not_2_out);
  nand nand_8 (nand_8_out, not_3_out, nand_4_out, not_1_out);
  LED Q (.in(nand_5_out));
  LED Q_2 (.in(nand_7_out));
endmodule

module Flip_Flop_Toggle__T (
  input  T
);

  wire CLEAR_out, clock_1_out, nand_1_out, nand_2_out, nand_3_out, nand_4_out, nand_5_out, nand_6_out,
       nand_7_out, nand_8_out, not_1_out, not_2_out, not_3_out, PRESET_out;

  Clock clock_1 (.out(clock_1_out));
  Button PRESET (.out(PRESET_out));
  not not_1 (not_1_out, PRESET_out);
  nand nand_1 (nand_1_out, nand_7_out, T, clock_1_out);
  nand nand_2 (nand_2_out, clock_1_out, T, nand_5_out);
  not not_2 (not_2_out, CLEAR_out);
  Button CLEAR (.out(CLEAR_out));
  nand nand_3 (nand_3_out, not_1_out, nand_1_out, nand_4_out);
  not not_3 (not_3_out, clock_1_out);
  nand nand_4 (nand_4_out, nand_3_out, nand_2_out, not_2_out);
  nand nand_5 (nand_5_out, not_1_out, nand_6_out, nand_7_out);
  nand nand_6 (nand_6_out, not_2_out, nand_3_out, not_3_out);
  nand nand_7 (nand_7_out, nand_5_out, nand_8_out, not_2_out);
  nand nand_8 (nand_8_out, not_3_out, nand_4_out, not_1_out);
  LED Q (.in(nand_5_out));
  LED Q_2 (.in(nand_7_out));
endmodule

module Flip_Flop_Data__D (
  input  D
);

  wire CLEAR_out, clock_1_out, nand_1_out, nand_2_out, nand_3_out, nand_4_out, nand_5_out, nand_6_out,
       nand_7_out, nand_8_out, not_1_out, not_2_out, not_3_out, not_4_out, PRESET_out;

  Clock clock_1 (.out(clock_1_out));
  not not_1 (not_1_out, D);
  not not_2 (not_2_out, PRESET_out);
  Button PRESET (.out(PRESET_out));
  nand nand_1 (nand_1_out, nand_8_out, D, clock_1_out);
  nand nand_2 (nand_2_out, clock_1_out, not_1_out, nand_6_out);
  Button CLEAR (.out(CLEAR_out));
  not not_3 (not_3_out, CLEAR_out);
  nand nand_3 (nand_3_out, not_2_out, nand_1_out, nand_4_out);
  not not_4 (not_4_out, clock_1_out);
  nand nand_4 (nand_4_out, nand_3_out, nand_2_out, not_3_out);
  nand nand_5 (nand_5_out, not_3_out, nand_3_out, not_4_out);
  nand nand_6 (nand_6_out, not_2_out, nand_5_out, nand_8_out);
  nand nand_7 (nand_7_out, not_4_out, nand_4_out, not_2_out);
  nand nand_8 (nand_8_out, nand_6_out, nand_7_out, not_3_out);
  LED Q (.in(nand_6_out));
  LED Q_2 (.in(nand_8_out));
endmodule
