// Logisim project main.circ as structural Verilog: 1 circuit, main circuit main
module main (
  input  J,
  input  K,
  output out_3,
  output out_4
);

  wire CLOCK_out, nand_1_out, nand_2_out, nand_3_out, nand_4_out, nand_5_out, nand_6_out, not_1_out;

  Clock CLOCK (.out(CLOCK_out));
  nand nand_1 (nand_1_out, J, CLOCK_out, out_4);
  not not_1 (not_1_out, CLOCK_out);
  nand nand_2 (nand_2_out, out_3, CLOCK_out, K);
  nand nand_3 (nand_3_out, nand_1_out, nand_4_out);
  nand nand_4 (nand_4_out, nand_3_out, nand_2_out);
  nand nand_5 (nand_5_out, nand_3_out, not_1_out);
  nand nand_6 (nand_6_out, not_1_out, nand_4_out);
  nand nand_7 (out_3, nand_5_out, out_4);
  nand nand_8 (out_4, out_3, nand_6_out);
endmodule
